// Logisim project Conte-200-Pipeline_Final (2).circ as structural Verilog: 14 circuits, main circuit main
// WB
module main (
  input  CLEAR,
  output [31:0] out_2,
  output [31:0] out_3,
  output out_4,
  output [31:0] out_5,
  output [3:0] WB_Data,
  output [3:0] WB_Data_2,
  output WB_Data_3,
  output out_9,
  output [3:0] out_10,
  output [3:0] out_11,
  output [31:0] WB_Data_4,
  output [31:0] out_13,
  output [31:0] out_14,
  output [3:0] out_15,
  output [31:0] out_16,
  output [3:0] out_17
);

  wire and_1_out, CLK, comparator_1_eq, comparator_2_eq, comparator_3_eq, comparator_4_eq, comparator_5_eq,
       comparator_6_eq, comparator_7_eq, comparator_8_eq, comparator_9_eq, EN, ForwardReg1Sel,
       ForwardReg2Sel, if_stage_1_should_flush, NoOp, or_1_out, or_2_out, or_3_out;
  wire [3:0] ex_mem_buffer_1_opcode_out, ex_mem_buffer_1_rx_out, EX_Opcode, FWD_REGNO1, FWD_REGNO2,
       idrr_ex_buffer_1_opcode_out, idrr_ex_buffer_1_rx_out, IDRR_Opcode_t, IDRR_Rx, IDRR_Ry, IDRR_Rz,
       MEM_Rx, mem_wb_buffer_1_rx_out, multiplexer_6_out, multiplexer_9_out, WB_Opcode;
  wire [4:0] id_rr_stage_1_pc_selector_id_rr;
  wire [31:0] ex_mem_buffer_1_rdata1_out, ex_mem_buffer_1_rdata2_out, ex_stage_1_rdata1_ex_2,
       ex_stage_1_rdata2_ex_2, id_rr_stage_1_call_pc_value__tr, id_rr_stage_1_goto_pc_value_pcaddr24,
       id_rr_stage_1_halt_enabled_id_rr, id_rr_stage_1_offset20_id_rr, id_rr_stage_1_pc_id_rr_out,
       id_rr_stage_1_pcaddr24_id_rr, id_rr_stage_1_ret_pc_value__ra, id_rr_stage_1_skp_pc_value,
       idrr_ex_buffer_1_offset_out, idrr_ex_buffer_1_pc_out, idrr_ex_buffer_1_rdata1_out,
       idrr_ex_buffer_1_rdata2_out, IDRR_ROut1, IDRR_ROut2, if_idrr_buffer_1_pc_out, if_stage_1_pc_1,
       MEM_Result, multiplexer_3_out, multiplexer_4_out, multiplexer_5_out, multiplexer_7_out, WB_Result;

  IF_Stage if_stage_1 (
    .CLK(CLK), .EN(EN), .CLEAR(CLEAR), .Instruction(out_13),
    .GOTO_PC_Value_PCaddr24(id_rr_stage_1_goto_pc_value_pcaddr24),
    .PC_SELECTOR(id_rr_stage_1_pc_selector_id_rr), .SHOULD_FLUSH(if_stage_1_should_flush),
    .RET_PC_Value__ra(id_rr_stage_1_ret_pc_value__ra), .CALL_PC_Value__tr(id_rr_stage_1_call_pc_value__tr),
    .HALT_Enabled(id_rr_stage_1_halt_enabled_id_rr), .SKP_PC_Value(id_rr_stage_1_skp_pc_value),
    .PC_1(if_stage_1_pc_1));  // open: out_14, out_11
  IF_IDRR_Buffer if_idrr_buffer_1 (
    .CLK(CLK), .FLUSH(if_stage_1_should_flush), .EN(EN), .PC_In(if_stage_1_pc_1), .Instruction_In(out_13),
    .PC_Out(if_idrr_buffer_1_pc_out), .Instruction_Output(out_16), .FLUSH_OUT(out_9));
  ID_RR_Stage id_rr_stage_1 (
    .Instruction_ID_RR_In(out_16), .PC_ID_RR_In(if_idrr_buffer_1_pc_out), .CLK(CLK),
    .PC_SELECTOR_ID_RR(id_rr_stage_1_pc_selector_id_rr), .EN(EN), .CLEAR(CLEAR),
    .Offset20_ID_RR(id_rr_stage_1_offset20_id_rr), .WB(WB_Data_3), .REG_WB(out_15),
    .PCaddr24_ID_RR(id_rr_stage_1_pcaddr24_id_rr), .WB_Data(WB_Result), .OUT_1_ID_RR(IDRR_ROut1),
    .OUT_2_ID_RR(IDRR_ROut2), .Opcode_ID_RR(out_10), .PC_ID_RR_Out(id_rr_stage_1_pc_id_rr_out),
    .RX_ID_RR(IDRR_Rx), .RY_ID_RR(IDRR_Ry), .GOTO_PC_Value_PCaddr24(id_rr_stage_1_goto_pc_value_pcaddr24),
    .RET_PC_Value__ra(id_rr_stage_1_ret_pc_value__ra), .CALL_PC_Value__tr(id_rr_stage_1_call_pc_value__tr),
    .SKP_PC_Value(id_rr_stage_1_skp_pc_value), .HALT_Enabled_ID_RR(id_rr_stage_1_halt_enabled_id_rr),
    .RZ_ID_RR(IDRR_Rz), .ForwardReg1Sel(ForwardReg1Sel), .ForwardReg1Value(out_2),
    .ForwardReg2Sel(ForwardReg2Sel), .ForwardReg2Value(out_3));
  Comparator #(.width(4)) comparator_1 (.a(IDRR_Opcode_t), .b(4'b1001), .eq(comparator_1_eq));  // open: gt, lt
  or or_1 (or_1_out, comparator_1_eq, comparator_2_eq);
  Comparator #(.width(4)) comparator_2 (.a(IDRR_Opcode_t), .b(4'b1100), .eq(comparator_2_eq));  // open: gt, lt
  Multiplexer #(.width(4), .enable("false")) multiplexer_1 (
    .in0(IDRR_Rz), .in1(IDRR_Rx), .out(FWD_REGNO2), .sel(or_1_out));
  Forwarding_Unit forwarding_unit_1 (
    .EX_Rx(out_17), .MEM_Rx(MEM_Rx), .WB_Rx(out_15), .WB_Result(WB_Result), .EX_Result(out_14),
    .MEM_Result(MEM_Result), .IDRR_Ry(FWD_REGNO1), .WB_OPCODE(WB_Opcode), .IDRR_Rz(FWD_REGNO2),
    .EX_OPCODE(EX_Opcode), .MEM_OPCODE(out_11), .IDRR_Opcode(out_10), .IDRR_Rx(IDRR_Rx),
    .IDRR_Rout1(IDRR_ROut1), .IDRR_Rout2(IDRR_ROut2), .ForwardReg1Sel(ForwardReg1Sel),
    .ForwardReg2Sel(ForwardReg2Sel), .Ry_FOut(out_2), .Rz_FOut(out_3));  // open: out_21, out_20
  Comparator #(.width(4)) comparator_3 (.a(IDRR_Opcode_t), .b(4'b1101), .eq(comparator_3_eq));  // open: gt, lt
  IDRR_EX_Buffer idrr_ex_buffer_1 (
    .CLK(CLK), .CLEAR(CLEAR), .PC_In(id_rr_stage_1_pc_id_rr_out), .OFFSET_IN(id_rr_stage_1_offset20_id_rr),
    .RData1_IN(IDRR_ROut1), .RData2_IN(IDRR_ROut2), .PCADDR24_IN(id_rr_stage_1_pcaddr24_id_rr),
    .OPCODE_OUT(idrr_ex_buffer_1_opcode_out), .PC_Out(idrr_ex_buffer_1_pc_out),
    .OFFSET_OUT(idrr_ex_buffer_1_offset_out), .RData1_OUT(idrr_ex_buffer_1_rdata1_out),
    .RData2_OUT(idrr_ex_buffer_1_rdata2_out), .RX_IN(IDRR_Rx), .RX_OUT(idrr_ex_buffer_1_rx_out),
    .OPCODE_IN(out_10), .RY_IN(IDRR_Ry), .EN(EN));  // open: PCADDR24_OUT, RY_OUT
  Multiplexer #(.width(4), .enable("false")) multiplexer_2 (
    .in0(IDRR_Ry), .in1(4'b1111), .out(FWD_REGNO1), .sel(comparator_3_eq));
  Multiplexer #(.width(32), .enable("false")) multiplexer_3 (
    .in0(idrr_ex_buffer_1_offset_out), .in1({32{1'b0}}), .out(multiplexer_3_out), .sel(NoOp));
  Multiplexer #(.width(32), .enable("false")) multiplexer_4 (
    .in0(idrr_ex_buffer_1_rdata1_out), .in1({32{1'b0}}), .out(multiplexer_4_out), .sel(NoOp));
  Multiplexer #(.width(32), .enable("false")) multiplexer_5 (
    .in0(idrr_ex_buffer_1_rdata2_out), .in1({32{1'b0}}), .out(multiplexer_5_out), .sel(NoOp));
  Multiplexer #(.width(4), .enable("false")) multiplexer_6 (
    .in0(idrr_ex_buffer_1_opcode_out), .in1(4'b0000), .out(multiplexer_6_out), .sel(NoOp));
  Multiplexer #(.width(32), .enable("false")) multiplexer_7 (
    .in0(idrr_ex_buffer_1_pc_out), .in1({32{1'b0}}), .out(multiplexer_7_out), .sel(NoOp));
  Multiplexer #(.disabled(0), .enable("false")) multiplexer_8 (.in0(1'b1), .in1(1'b0), .out(EN), .sel(out_4));
  Multiplexer #(.width(4), .enable("false")) multiplexer_9 (
    .in0(idrr_ex_buffer_1_rx_out), .in1(4'b0000), .out(multiplexer_9_out), .sel(NoOp));
  Comparator #(.width(4), .mode("unsigned")) comparator_4 (
    .a(EX_Opcode), .b(4'b1000), .eq(comparator_4_eq));  // open: gt, lt
  Comparator #(.width(4), .mode("unsigned")) comparator_5 (
    .a(out_17), .b(FWD_REGNO1), .eq(comparator_5_eq));  // open: gt, lt
  Comparator #(.width(4), .mode("unsigned")) comparator_6 (
    .a(out_17), .b(FWD_REGNO2), .eq(comparator_6_eq));  // open: gt, lt
  Comparator #(.width(4), .mode("unsigned")) comparator_7 (
    .a(out_10), .b(4'b0000), .eq(comparator_7_eq));  // open: gt, lt
  Comparator #(.width(4), .mode("unsigned")) comparator_8 (
    .a(out_10), .b(4'b0010), .eq(comparator_8_eq));  // open: gt, lt
  Comparator #(.width(4), .mode("unsigned")) comparator_9 (
    .a(out_10), .b(4'b0011), .eq(comparator_9_eq));  // open: gt, lt
  Clock CLOCK (.out(CLK));
  EX_Stage ex_stage_1 (
    .RDATA1_EX(multiplexer_4_out), .EX_RESULT(out_14), .RDATA2_EX(multiplexer_5_out),
    .Opcode_EX(multiplexer_6_out), .RDATA1_EX_2(ex_stage_1_rdata1_ex_2),
    .RDATA2_EX_2(ex_stage_1_rdata2_ex_2), .Opcode_EX_2(EX_Opcode), .RX_EX_2(out_17),
    .RX_EX(multiplexer_9_out), .OFFSET_EX(multiplexer_3_out));  // open: OFFSET_EX_2
  or or_2 (or_2_out, comparator_7_eq, comparator_8_eq, comparator_9_eq);
  EX_MEM_Buffer ex_mem_buffer_1 (
    .CLEAR(CLEAR), .EN(1'b1), .PC_IN(multiplexer_7_out), .CLK(CLK), .RESULT_IN(out_14),
    .OPCODE_IN(EX_Opcode), .RX_IN(out_17), .Rdata1_IN(ex_stage_1_rdata1_ex_2),
    .Rdata2_IN(ex_stage_1_rdata2_ex_2), .RESULT_OUT(out_5), .OPCODE_OUT(ex_mem_buffer_1_opcode_out),
    .RX_OUT(ex_mem_buffer_1_rx_out), .Rdata1_OUT(ex_mem_buffer_1_rdata1_out),
    .Rdata2_OUT(ex_mem_buffer_1_rdata2_out));  // open: RY_IN, PC_OUT, RY_OUT
  and and_1 (and_1_out, comparator_6_eq, or_2_out);
  MEM_Stage mem_stage_1 (
    .CLK(CLK), .Opcode_MEM(ex_mem_buffer_1_opcode_out), .RX_MEM(ex_mem_buffer_1_rx_out),
    .RDATA2_MEM_In(ex_mem_buffer_1_rdata2_out), .RAM_MEM_OUT(MEM_Result), .Opcode_MEM_OUT(out_11),
    .RX_MEM_OUT(MEM_Rx), .RESULT_MEM_In(out_5), .RDATA1_MEM_In(ex_mem_buffer_1_rdata1_out));  // open: RY_MEM
  or or_3 (or_3_out, comparator_5_eq, and_1_out);
  Register #(.width(1)) register_1 (.D(out_4), .Q(NoOp), .clk(CLK));  // open: en, clr
  MEM_WB_Buffer mem_wb_buffer_1 (
    .CLK(CLK), .RAM_IN(MEM_Result), .OPCODE_IN(out_11), .RX_IN(MEM_Rx), .RAM_OUT(WB_Data_4),
    .OPCODE_OUT(WB_Data), .RX_OUT(mem_wb_buffer_1_rx_out), .EN(1'b1));  // open: CLEAR, RESULT_IN, RESULT_OUT
  and and_2 (out_4, comparator_4_eq, or_3_out);
  WB_Stage wb_stage_1 (
    .OPCODE_WB(WB_Data), .RX(mem_wb_buffer_1_rx_out), .WB_Data_2(WB_Result), .REG_WB(out_15),
    .WB_Data(WB_Data_4), .WB(WB_Data_3), .CLK(CLK), .OPCODE_WB_OUT(WB_Opcode));

  assign WB_Data_2 = out_15;

  // Other names for the same wires on the sheet: EX_Result[31:0] = out_14; EX_Rx[3:0] = out_17; FLUSH = out_9;
  //   IDRR_Opcode[3:0] = out_10; MEM_Opcode[3:0] = out_11; RyFOut[31:0] = out_2; RzFOut[31:0] = out_3; STALL = out_4;
  //   WB_Rx[3:0] = out_15

  // Notes on the sheet:
  //   Ashwini Iyer's Pipeline
endmodule

module Dual_Ported_Register_File (
  input  CLK,
  input  WrEN,
  input  [3:0] WrREGNO,
  input  [3:0] RdREGNO1,
  input  [3:0] RdREGNO2,
  input  [31:0] INPUT,
  output [31:0] OUT1,
  output [31:0] OUT2
);

  wire En_a0, En_a1, En_a2, En_at, En_fp, En_k0, En_ra, En_s0, En_s1, En_s2, En_sp, En_t0, En_t1, En_t2,
       En_v0;
  wire [31:0] a0, a1, a2, at, fp, k0, ra, s0, s1, s2, sp, t0, t1, t2, v0, zero;

  Decoder #(.select(4), .disabled(0)) decoder_1 (
    .out1(En_at), .out2(En_v0), .out3(En_a0), .out4(En_a1), .out5(En_a2), .out6(En_t0), .out7(En_t1),
    .out8(En_t2), .out9(En_s0), .out10(En_s1), .out11(En_s2), .out12(En_k0), .out13(En_sp), .out14(En_fp),
    .out15(En_ra), .sel(WrREGNO), .en(WrEN));  // open: out0
  Register #(.width(32)) u_zero (.D(INPUT), .en(1'b0), .Q(zero), .clk(CLK));  // open: clr
  Register #(.width(32)) u_at (.D(INPUT), .en(En_at), .Q(at), .clk(CLK));  // open: clr
  Register #(.width(32)) u_v0 (.D(INPUT), .en(En_v0), .Q(v0), .clk(CLK));  // open: clr
  Register #(.width(32)) u_a0 (.D(INPUT), .en(En_a0), .Q(a0), .clk(CLK));  // open: clr
  Register #(.width(32)) u_a1 (.D(INPUT), .en(En_a1), .Q(a1), .clk(CLK));  // open: clr
  Register #(.width(32)) u_a2 (.D(INPUT), .en(En_a2), .Q(a2), .clk(CLK));  // open: clr
  Register #(.width(32)) u_t0 (.D(INPUT), .en(En_t0), .Q(t0), .clk(CLK));  // open: clr
  Register #(.width(32)) u_t1 (.D(INPUT), .en(En_t1), .Q(t1), .clk(CLK));  // open: clr
  Multiplexer #(.select(4), .width(32), .disabled(0), .enable("false")) multiplexer_1 (
    .in0(zero), .in1(at), .in2(v0), .in3(a0), .in4(a1), .in5(a2), .in6(t0), .in7(t1), .in8(t2), .in9(s0),
    .in10(s1), .in11(s2), .in12(k0), .in13(sp), .in14(fp), .in15(ra), .out(OUT2), .sel(RdREGNO2));
  Register #(.width(32)) u_t2 (.D(INPUT), .en(En_t2), .Q(t2), .clk(CLK));  // open: clr
  Register #(.width(32)) u_s0 (.D(INPUT), .en(En_s0), .Q(s0), .clk(CLK));  // open: clr
  Register #(.width(32)) u_s1 (.D(INPUT), .en(En_s1), .Q(s1), .clk(CLK));  // open: clr
  Register #(.width(32)) u_s2 (.D(INPUT), .en(En_s2), .Q(s2), .clk(CLK));  // open: clr
  Register #(.width(32)) u_k0 (.D(INPUT), .en(En_k0), .Q(k0), .clk(CLK));  // open: clr
  Register #(.width(32)) u_sp (.D(INPUT), .en(En_sp), .Q(sp), .clk(CLK));  // open: clr
  Register #(.width(32)) u_fp (.D(INPUT), .en(En_fp), .Q(fp), .clk(CLK));  // open: clr
  Register #(.width(32)) u_ra (.D(INPUT), .en(En_ra), .Q(ra), .clk(CLK));  // open: clr
  Multiplexer #(.select(4), .width(32), .disabled(0), .enable("false")) multiplexer_2 (
    .in0(zero), .in1(at), .in2(v0), .in3(a0), .in4(a1), .in5(a2), .in6(t0), .in7(t1), .in8(t2), .in9(s0),
    .in10(s1), .in11(s2), .in12(k0), .in13(sp), .in14(fp), .in15(ra), .out(OUT1), .sel(RdREGNO1));

  // Notes on the sheet:
  //   MODIFY AT YOUR OWN RISK
endmodule

// IF/IDRR
module IF_IDRR_Buffer (
  input  CLK,
  input  FLUSH,
  input  EN,
  input  [31:0] PC_In,
  input  [31:0] Instruction_In,
  output [31:0] PC_Out,
  output [31:0] Instruction_Output,
  output FLUSH_OUT
);

  Register #(.width(32)) PC (.D(PC_In), .en(EN), .Q(PC_Out), .clk(CLK));  // open: clr
  Register #(.width(32)) Instruction (.D(Instruction_In), .en(EN), .Q(Instruction_Output), .clk(CLK));  // open: clr

  assign FLUSH_OUT = FLUSH;
endmodule

module IDRR_EX_Buffer (
  input  CLK,
  input  CLEAR,
  input  EN,
  input  [31:0] PC_In,
  input  [31:0] OFFSET_IN,
  input  [31:0] RData1_IN,
  input  [31:0] RData2_IN,
  input  [31:0] PCADDR24_IN,
  input  [3:0] OPCODE_IN,
  input  [3:0] RX_IN,
  input  [3:0] RY_IN,
  output [31:0] PC_Out,
  output [31:0] OFFSET_OUT,
  output [31:0] RData1_OUT,
  output [31:0] RData2_OUT,
  output [31:0] PCADDR24_OUT,
  output [3:0] OPCODE_OUT,
  output [3:0] RX_OUT,
  output [3:0] RY_OUT
);

  Register #(.width(32)) PC (.D(PC_In), .en(EN), .Q(PC_Out), .clk(CLK), .clr(CLEAR));
  Register #(.width(32)) Instruction (.D(OFFSET_IN), .en(EN), .Q(OFFSET_OUT), .clk(CLK), .clr(CLEAR));
  Register #(.width(32)) RData1 (.D(RData1_IN), .en(EN), .Q(RData1_OUT), .clk(CLK), .clr(CLEAR));
  Register #(.width(32)) RData2 (.D(RData2_IN), .en(EN), .Q(RData2_OUT), .clk(CLK), .clr(CLEAR));
  Register #(.width(32)) PCADDR24 (.D(PCADDR24_IN), .en(EN), .Q(PCADDR24_OUT), .clk(CLK), .clr(CLEAR));
  Register #(.width(4)) Opcode (.D(OPCODE_IN), .en(EN), .Q(OPCODE_OUT), .clk(CLK), .clr(CLEAR));
  Register #(.width(4)) Rx (.D(RX_IN), .en(EN), .Q(RX_OUT), .clk(CLK), .clr(CLEAR));
  Register #(.width(4)) RY (.D(RY_IN), .en(EN), .Q(RY_OUT), .clk(CLK), .clr(CLEAR));
endmodule

// EX/MEM
module EX_MEM_Buffer (
  input  CLEAR,
  input  EN,
  input  [31:0] PC_IN,
  input  CLK,
  input  [31:0] RESULT_IN,
  input  [3:0] OPCODE_IN,
  input  [3:0] RX_IN,
  input  [3:0] RY_IN,
  input  [31:0] Rdata1_IN,
  input  [31:0] Rdata2_IN,
  output [31:0] PC_OUT,
  output [31:0] RESULT_OUT,
  output [3:0] OPCODE_OUT,
  output [3:0] RX_OUT,
  output [3:0] RY_OUT,
  output [31:0] Rdata1_OUT,
  output [31:0] Rdata2_OUT
);

  Register #(.width(32)) PC (.D(PC_IN), .Q(PC_OUT), .clk(CLK), .clr(CLEAR));  // open: en
  Register #(.width(32)) RESULT (.D(RESULT_IN), .Q(RESULT_OUT), .clk(CLK), .clr(CLEAR));  // open: en
  Register #(.width(4)) Opcode (.D(OPCODE_IN), .Q(OPCODE_OUT), .clk(CLK), .clr(CLEAR));  // open: en
  Register #(.width(4)) Rx (.D(RX_IN), .Q(RX_OUT), .clk(CLK), .clr(CLEAR));  // open: en
  Register #(.width(4)) RY (.D(RY_IN), .Q(RY_OUT), .clk(CLK), .clr(CLEAR));  // open: en
  Register #(.width(32)) Rdata1 (.D(Rdata1_IN), .en(EN), .Q(Rdata1_OUT), .clk(CLK), .clr(CLEAR));
  Register #(.width(32)) Rdata2 (.D(Rdata2_IN), .en(EN), .Q(Rdata2_OUT), .clk(CLK), .clr(CLEAR));
endmodule

// MEM/WB
module MEM_WB_Buffer (
  input  CLEAR,
  input  EN,
  input  [31:0] RESULT_IN,
  input  CLK,
  input  [31:0] RAM_IN,
  input  [3:0] OPCODE_IN,
  input  [3:0] RX_IN,
  output [31:0] RESULT_OUT,
  output [31:0] RAM_OUT,
  output [3:0] OPCODE_OUT,
  output [3:0] RX_OUT
);

  Register #(.width(32)) RESULT (.D(RESULT_IN), .en(EN), .Q(RESULT_OUT), .clk(CLK), .clr(CLEAR));
  Register #(.width(32)) RAM (.D(RAM_IN), .en(EN), .Q(RAM_OUT), .clk(CLK), .clr(CLEAR));
  Register #(.width(4)) Opcode (.D(OPCODE_IN), .en(EN), .Q(OPCODE_OUT), .clk(CLK), .clr(CLEAR));
  Register #(.width(4)) Rx (.D(RX_IN), .en(EN), .Q(RX_OUT), .clk(CLK), .clr(CLEAR));
endmodule

// Forwarding
module Forwarding_Unit (
  input  [3:0] EX_Rx,
  input  [3:0] MEM_Rx,
  input  [3:0] WB_Rx,
  input  [31:0] WB_Result,
  input  [31:0] EX_Result,
  input  [31:0] MEM_Result,
  input  [3:0] IDRR_Ry,
  input  [3:0] WB_OPCODE,
  input  [3:0] IDRR_Rz,
  input  [3:0] EX_OPCODE,
  input  [3:0] MEM_OPCODE,
  input  [3:0] IDRR_Opcode,
  input  [3:0] IDRR_Rx,
  input  [31:0] IDRR_Rout1,
  input  [31:0] IDRR_Rout2,
  output ForwardReg1Sel,
  output ForwardReg2Sel,
  output [31:0] Rz_FOut,
  output [31:0] Ry_FOut,
  output [1:0] out_20,
  output [1:0] out_21
);

  wire _0_Ry, _0_Rz, _1_Ry, _1_Rz, _2_Ry, _2_Rz, _3_Ry, _3_Rz, comparator_1_eq, comparator_2_eq,
       comparator_3_eq, comparator_4_eq, comparator_5_eq, comparator_6_eq, comparator_14_eq,
       comparator_15_eq, comparator_16_eq, comparator_17_eq, comparator_18_eq, comparator_19_eq,
       comparator_27_eq, comparator_28_eq, comparator_29_eq, comparator_30_eq, comparator_31_eq,
       comparator_32_eq, ENABLE_EX, ENABLE_MEM, ENABLE_WB, EX__FRy, EX__FRz, MEM__FRy, MEM__FRz, MEM_FORWARD,
       Ry_FORWARD_EX_Rx, Ry_FORWARD_MEM_Rx, Ry_FORWARD_WB_Rx, Ry_MEM_FORWARD, Rz_FORWARD_EX_Rx,
       Rz_FORWARD_MEM_Rx, Rz_FORWARD_WB_Rx, WB__FRy, WB__FRz;

  Comparator #(.width(4)) comparator_1 (.a(EX_OPCODE), .b(4'b0000), .eq(comparator_1_eq));  // open: gt, lt
  Comparator #(.width(4)) comparator_2 (.a(EX_OPCODE), .b(4'b0001), .eq(comparator_2_eq));  // open: gt, lt
  Comparator #(.width(4)) comparator_3 (.a(EX_OPCODE), .b(4'b0010), .eq(comparator_3_eq));  // open: gt, lt
  Comparator #(.width(4)) comparator_4 (.a(EX_OPCODE), .b(4'b0101), .eq(comparator_4_eq));  // open: gt, lt
  Comparator #(.width(4)) comparator_5 (.a(EX_OPCODE), .b(4'b1000), .eq(comparator_5_eq));  // open: gt, lt
  Comparator #(.width(4)) comparator_6 (.a(EX_OPCODE), .b(4'b1100), .eq(comparator_6_eq));  // open: gt, lt
  Comparator #(.width(4)) comparator_7 (.a(IDRR_Ry), .b(EX_Rx), .eq(EX__FRy));  // open: gt, lt
  Comparator #(.width(4)) comparator_8 (.a(IDRR_Rz), .b(EX_Rx), .eq(EX__FRz));  // open: gt, lt
  and and_1 (Ry_FORWARD_EX_Rx, ENABLE_EX, EX__FRy);
  and and_2 (Rz_FORWARD_EX_Rx, ENABLE_EX, EX__FRz);
  Comparator #(.width(3)) comparator_9 (
    .a({Rz_FORWARD_EX_Rx, Rz_FORWARD_MEM_Rx, Rz_FORWARD_WB_Rx}), .b(3'b000), .eq(_0_Rz));  // open: gt, lt
  Comparator #(.width(3)) comparator_10 (
    .a({Rz_FORWARD_EX_Rx, Rz_FORWARD_MEM_Rx, Rz_FORWARD_WB_Rx}), .b(3'b001), .eq(_1_Rz));  // open: gt, lt
  Comparator #(.width(3)) comparator_11 (
    .a({Rz_FORWARD_EX_Rx, Rz_FORWARD_MEM_Rx, Rz_FORWARD_WB_Rx}), .b(3'b010), .eq(_2_Rz));  // open: gt, lt
  Comparator #(.width(3)) comparator_12 (
    .a({Rz_FORWARD_EX_Rx, Rz_FORWARD_MEM_Rx, Rz_FORWARD_WB_Rx}), .b(3'b011), .eq(_3_Rz));  // open: gt, lt
  Comparator #(.width(2), .mode("unsigned")) comparator_13 (
    .a(out_20), .b(2'b00), .gt(ForwardReg2Sel));  // open: eq, lt
  or or_1 (ENABLE_EX, comparator_1_eq, comparator_2_eq, comparator_3_eq, comparator_4_eq, comparator_5_eq, comparator_6_eq);
  assign out_20 = _0_Rz ? 2'b00 : 2'bz;  // Controlled_Buffer controlled_buffer_1
  assign out_20 = Rz_FORWARD_EX_Rx ? 2'b01 : 2'bz;  // Controlled_Buffer controlled_buffer_2
  assign out_20 = MEM_FORWARD ? 2'b10 : 2'bz;  // Controlled_Buffer controlled_buffer_3
  assign out_20 = _1_Rz ? 2'b11 : 2'bz;  // Controlled_Buffer controlled_buffer_4
  Multiplexer #(.select(2), .width(32), .enable("false")) multiplexer_1 (
    .in0(IDRR_Rout2), .in1(EX_Result), .in2(MEM_Result), .in3(WB_Result), .out(Rz_FOut), .sel(out_20));
  or or_2 (MEM_FORWARD, _2_Rz, _3_Rz);
  and and_3 (Ry_FORWARD_MEM_Rx, ENABLE_MEM, MEM__FRy);
  and and_4 (Rz_FORWARD_MEM_Rx, ENABLE_MEM, MEM__FRz);
  Comparator #(.width(4)) comparator_14 (.a(MEM_OPCODE), .b(4'b0000), .eq(comparator_14_eq));  // open: gt, lt
  Comparator #(.width(4)) comparator_15 (.a(MEM_OPCODE), .b(4'b0001), .eq(comparator_15_eq));  // open: gt, lt
  Comparator #(.width(4)) comparator_16 (.a(MEM_OPCODE), .b(4'b0010), .eq(comparator_16_eq));  // open: gt, lt
  Comparator #(.width(4)) comparator_17 (.a(MEM_OPCODE), .b(4'b0101), .eq(comparator_17_eq));  // open: gt, lt
  Comparator #(.width(4)) comparator_18 (.a(MEM_OPCODE), .b(4'b1000), .eq(comparator_18_eq));  // open: gt, lt
  Comparator #(.width(4)) comparator_19 (.a(MEM_OPCODE), .b(4'b1100), .eq(comparator_19_eq));  // open: gt, lt
  Comparator #(.width(4)) comparator_20 (.a(IDRR_Ry), .b(MEM_Rx), .eq(MEM__FRy));  // open: gt, lt
  Comparator #(.width(4)) comparator_21 (.a(IDRR_Rz), .b(MEM_Rx), .eq(MEM__FRz));  // open: gt, lt
  or or_3 (ENABLE_MEM, comparator_14_eq, comparator_15_eq, comparator_16_eq, comparator_17_eq, comparator_18_eq, comparator_19_eq);
  Multiplexer #(.select(2), .width(32), .enable("false")) multiplexer_2 (
    .in0(IDRR_Rout1), .in1(EX_Result), .in2(MEM_Result), .in3(WB_Result), .out(Ry_FOut), .sel(out_21));
  and and_5 (Ry_FORWARD_WB_Rx, ENABLE_WB, WB__FRy);
  and and_6 (Rz_FORWARD_WB_Rx, ENABLE_WB, WB__FRz);
  Comparator #(.width(3)) comparator_22 (
    .a({Ry_FORWARD_EX_Rx, Ry_FORWARD_MEM_Rx, Ry_FORWARD_WB_Rx}), .b(3'b000), .eq(_0_Ry));  // open: gt, lt
  Comparator #(.width(3)) comparator_23 (
    .a({Ry_FORWARD_EX_Rx, Ry_FORWARD_MEM_Rx, Ry_FORWARD_WB_Rx}), .b(3'b001), .eq(_1_Ry));  // open: gt, lt
  Comparator #(.width(3)) comparator_24 (
    .a({Ry_FORWARD_EX_Rx, Ry_FORWARD_MEM_Rx, Ry_FORWARD_WB_Rx}), .b(3'b010), .eq(_2_Ry));  // open: gt, lt
  Comparator #(.width(3)) comparator_25 (
    .a({Ry_FORWARD_EX_Rx, Ry_FORWARD_MEM_Rx, Ry_FORWARD_WB_Rx}), .b(3'b011), .eq(_3_Ry));  // open: gt, lt
  assign out_21 = _0_Ry ? 2'b00 : 2'bz;  // Controlled_Buffer controlled_buffer_5
  assign out_21 = Ry_FORWARD_EX_Rx ? 2'b01 : 2'bz;  // Controlled_Buffer controlled_buffer_6
  assign out_21 = Ry_MEM_FORWARD ? 2'b10 : 2'bz;  // Controlled_Buffer controlled_buffer_7
  assign out_21 = _1_Ry ? 2'b11 : 2'bz;  // Controlled_Buffer controlled_buffer_8
  Comparator #(.width(2), .mode("unsigned")) comparator_26 (
    .a(out_21), .b(2'b00), .gt(ForwardReg1Sel));  // open: eq, lt
  Comparator #(.width(4)) comparator_27 (.a(WB_OPCODE), .b(4'b0000), .eq(comparator_27_eq));  // open: gt, lt
  Comparator #(.width(4)) comparator_28 (.a(WB_OPCODE), .b(4'b0001), .eq(comparator_28_eq));  // open: gt, lt
  Comparator #(.width(4)) comparator_29 (.a(WB_OPCODE), .b(4'b0010), .eq(comparator_29_eq));  // open: gt, lt
  Comparator #(.width(4)) comparator_30 (.a(WB_OPCODE), .b(4'b0101), .eq(comparator_30_eq));  // open: gt, lt
  Comparator #(.width(4)) comparator_31 (.a(WB_OPCODE), .b(4'b1000), .eq(comparator_31_eq));  // open: gt, lt
  Comparator #(.width(4)) comparator_32 (.a(WB_OPCODE), .b(4'b1100), .eq(comparator_32_eq));  // open: gt, lt
  Comparator #(.width(4)) comparator_33 (.a(IDRR_Ry), .b(WB_Rx), .eq(WB__FRy));  // open: gt, lt
  Comparator #(.width(4)) comparator_34 (.a(IDRR_Rz), .b(WB_Rx), .eq(WB__FRz));  // open: gt, lt
  or or_4 (Ry_MEM_FORWARD, _2_Ry, _3_Ry);
  or or_5 (ENABLE_WB, comparator_27_eq, comparator_28_eq, comparator_29_eq, comparator_30_eq, comparator_31_eq, comparator_32_eq);

  // Other names for the same wires on the sheet: IDDR_Rx[3:0] = IDRR_Rx; Ry[1:0] = out_21; Rz[1:0] = out_20
endmodule

module ALU (
  input  [1:0] in_1,
  input  [31:0] A,
  input  [31:0] B,
  output [31:0] out_4
);

  wire [31:0] adder_1_out, adder_2_out, nand_1_out, subtractor_1_out;

  Adder #(.width(32)) adder_1 (.a(A), .b(B), .out(adder_1_out));  // open: cin, cout
  Subtractor #(.width(32)) subtractor_1 (.a(A), .b(B), .out(subtractor_1_out));  // open: bin, bout
  assign nand_1_out = ~(A & B);  // NAND_Gate nand_1, 32 bits wide
  Adder #(.width(32)) adder_2 (.a(A), .b(32'h1), .out(adder_2_out));  // open: cin, cout
  Multiplexer #(.select(2), .width(32), .disabled(0), .enable("false")) multiplexer_1 (
    .in0(adder_1_out), .in1(subtractor_1_out), .in2(nand_1_out), .in3(adder_2_out), .out(out_4), .sel(in_1));

  // Other names for the same wires on the sheet: func[1:0] = in_1; output[31:0] = out_4
endmodule

// IF
module IF_Stage (
  input  CLK,
  input  EN,
  input  CLEAR,
  input  [31:0] SKP_PC_Value,
  input  [31:0] GOTO_PC_Value_PCaddr24,
  input  [31:0] RET_PC_Value__ra,
  input  [31:0] CALL_PC_Value__tr,
  input  [31:0] HALT_Enabled,
  input  [4:0] PC_SELECTOR,
  output [31:0] PC_1,
  output [31:0] out_11,
  output [31:0] Instruction,
  output SHOULD_FLUSH,
  output [4:0] out_14
);

  wire comparator_1_eq, comparator_2_eq, comparator_3_eq, comparator_4_eq, comparator_5_eq;
  wire [23:0] bit_extender_1_out;
  wire [31:0] Instruction_t, multiplexer_1_out, PC_1_t, PC_q;

  Comparator #(.width(1), .mode("unsigned")) comparator_1 (
    .a(PC_SELECTOR[0]), .b(1'b1), .eq(comparator_1_eq));  // open: gt, lt
  Comparator #(.width(1), .mode("unsigned")) comparator_2 (
    .a(PC_SELECTOR[1]), .b(1'b1), .eq(comparator_2_eq));  // open: gt, lt
  Comparator #(.width(1), .mode("unsigned")) comparator_3 (
    .a(PC_SELECTOR[2]), .b(1'b1), .eq(comparator_3_eq));  // open: gt, lt
  Comparator #(.width(1), .mode("unsigned")) comparator_4 (
    .a(PC_SELECTOR[3]), .b(1'b1), .eq(comparator_4_eq));  // open: gt, lt
  Comparator #(.width(1), .mode("unsigned")) comparator_5 (
    .a(PC_SELECTOR[4]), .b(1'b1), .eq(comparator_5_eq));  // open: gt, lt
  or or_1 (SHOULD_FLUSH, comparator_1_eq, comparator_2_eq, comparator_3_eq, comparator_4_eq, comparator_5_eq);
  Multiplexer #(.select(5), .width(32), .disabled(0), .enable("false")) multiplexer_1 (
    .in0(PC_1_t), .in1(SKP_PC_Value), .in2(GOTO_PC_Value_PCaddr24), .in4(CALL_PC_Value__tr),
    .in8(RET_PC_Value__ra), .in16(HALT_Enabled), .out(multiplexer_1_out), .sel(PC_SELECTOR));  // open: in3, in5, in6, in7, in9, in10, in11, in12, in13, in14, in15, in17, in18, in19, in20, in21, in22, in23, in24, in25, in26, in27, in28, in29, in30, in31
  Register #(.width(32)) PC (.D(multiplexer_1_out), .en(EN), .Q(PC_q), .clk(CLK));  // open: clr
  Bit_Extender #(.in_width(32), .out_width(24), .\type ("sign")) bit_extender_1 (.in(PC_q), .out(bit_extender_1_out));
  Adder #(.width(32)) adder_1 (.a(PC_q), .b(32'h1), .out(PC_1_t));  // open: cin, cout
  ROM #(.addrWidth(24), .dataWidth(32)) rom_1 (.addr(bit_extender_1_out), .data(Instruction_t), .sel(EN));
  Multiplexer #(.width(32), .disabled(0), .enable("false")) multiplexer_2 (
    .in0(PC_1_t), .in1({32{1'b0}}), .out(PC_1), .sel(SHOULD_FLUSH));
  Multiplexer #(.width(32), .disabled(0), .enable("false")) multiplexer_3 (
    .in0(Instruction_t), .in1({32{1'b0}}), .out(Instruction), .sel(SHOULD_FLUSH));

  assign out_11 = GOTO_PC_Value_PCaddr24;
  assign out_14 = PC_SELECTOR;

  // Other names for the same wires on the sheet: FLUSH = SHOULD_FLUSH

  // Notes on the sheet:
  //   contents of rom_1 (hex, n*v repeats v):
  //   5d00002f 8dd00000 5300000b 83300000 5400000c 84400000 5100000e c1000000 5300000d 92300000 f0000000 2
  //   a 0 1ddfffff 9ed00000 1ed00000 30400000 40000022 30300000 40000024 144fffff 5100000e 1ddffffe
  //   9fefffff 93effffe c1000000 4200000 83effffe 51000028 c1000000 8fefffff 1dd00002 40000025 12000001
  //   31000002 2000000 8ee00000 1dd00001 d0000000 2000000 16000001 2200003 16600001 31600004 d0000000
  //   4000002a a00000
endmodule

// ID/RR
module ID_RR_Stage (
  input  CLK,
  input  ForwardReg1Sel,
  input  EN,
  input  CLEAR,
  input  WB,
  input  [31:0] ForwardReg1Value,
  input  [3:0] REG_WB,
  input  [31:0] WB_Data,
  input  ForwardReg2Sel,
  input  [31:0] Instruction_ID_RR_In,
  input  [31:0] ForwardReg2Value,
  input  [31:0] PC_ID_RR_In,
  output [4:0] PC_SELECTOR_ID_RR,
  output [31:0] Offset20_ID_RR,
  output [31:0] SKP_PC_Value,
  output [31:0] PCaddr24_ID_RR,
  output [31:0] GOTO_PC_Value_PCaddr24,
  output [31:0] OUT_1_ID_RR,
  output [31:0] OUT_2_ID_RR,
  output [31:0] RET_PC_Value__ra,
  output [3:0] Opcode_ID_RR,
  output [31:0] PC_ID_RR_Out,
  output [31:0] CALL_PC_Value__tr,
  output [3:0] RX_ID_RR,
  output [3:0] RY_ID_RR,
  output [3:0] RZ_ID_RR,
  output [31:0] HALT_Enabled_ID_RR
);

  wire ADD_ID_RR, ADDI_ID_RR, comparator_1_eq, comparator_1_gt, comparator_1_lt, I_Type, LEA_ID_RR, LW_ID_RR,
       NAND_ID_RR, not_1_out, not_2_out, not_3_out, or_3_out, or_4_out, or_5_out, R_Type, SKP__ID_RR,
       SKP_ID_RR, SW_ID_RR;
  wire [3:0] REGNO1_ID_RR, REGNO2_ID_RR;
  wire [31:0] dual_ported_register_file_1_out1, dual_ported_register_file_1_out2, multiplexer_5_out;

  or or_1 (R_Type, ADD_ID_RR, NAND_ID_RR, SKP_ID_RR);
  and and_1 (PC_SELECTOR_ID_RR[0], SKP__ID_RR, SKP_ID_RR);
  Adder #(.width(32)) adder_1 (.a(PC_ID_RR_In), .b(32'h1), .out(SKP_PC_Value));  // open: cin, cout
  Subtractor #(.width(32)) subtractor_1 (.a(PC_ID_RR_In), .b(32'h1), .out(HALT_Enabled_ID_RR));  // open: bin, bout
  or or_2 (I_Type, ADDI_ID_RR, LW_ID_RR);
  assign Offset20_ID_RR = {{12{Instruction_ID_RR_In[19]}}, Instruction_ID_RR_In[19:0]};  // Bit_Extender bit_extender_1
  assign GOTO_PC_Value_PCaddr24 = {{8{1'b0}}, Instruction_ID_RR_In[23:0]};  // Bit_Extender bit_extender_2
  Multiplexer #(.width(4), .disabled(0), .enable("false")) multiplexer_1 (
    .in0(Instruction_ID_RR_In[23:20]), .in1(4'b1111), .out(REGNO1_ID_RR), .sel(PC_SELECTOR_ID_RR[3]));
  Decoder #(.select(4), .enable("false")) decoder_1 (
    .out0(ADD_ID_RR), .out1(ADDI_ID_RR), .out2(NAND_ID_RR), .out3(SKP_ID_RR), .out4(PC_SELECTOR_ID_RR[1]),
    .out5(LEA_ID_RR), .out8(LW_ID_RR), .out9(SW_ID_RR), .out12(PC_SELECTOR_ID_RR[2]),
    .out13(PC_SELECTOR_ID_RR[3]), .out15(PC_SELECTOR_ID_RR[4]), .sel(Instruction_ID_RR_In[31:28]));  // open: out6, out7, out10, out11, out14
  Multiplexer #(.width(4), .disabled(0), .enable("false")) multiplexer_2 (
    .in0(Instruction_ID_RR_In[3:0]), .in1(Instruction_ID_RR_In[27:24]), .out(REGNO2_ID_RR), .sel(or_3_out));
  or or_3 (or_3_out, SW_ID_RR, PC_SELECTOR_ID_RR[2]);
  not not_1 (not_1_out, ForwardReg1Sel);
  Dual_Ported_Register_File dual_ported_register_file_1 (
    .CLK(CLK), .WrEN(WB), .OUT1(dual_ported_register_file_1_out1), .WrREGNO(REG_WB), .RdREGNO1(REGNO1_ID_RR),
    .RdREGNO2(REGNO2_ID_RR), .OUT2(dual_ported_register_file_1_out2), .INPUT(WB_Data));
  Multiplexer #(.width(32), .disabled(0), .enable("false")) multiplexer_3 (
    .in0(ForwardReg1Value), .in1(dual_ported_register_file_1_out1), .out(RET_PC_Value__ra), .sel(not_1_out));
  Multiplexer #(.width(32), .disabled(0), .enable("false")) multiplexer_4 (
    .in0(dual_ported_register_file_1_out2), .in1(ForwardReg2Value), .out(CALL_PC_Value__tr),
    .sel(ForwardReg2Sel));
  Comparator #(.width(32), .mode("unsigned")) comparator_1 (
    .a(RET_PC_Value__ra), .b(CALL_PC_Value__tr), .gt(comparator_1_gt), .eq(comparator_1_eq),
    .lt(comparator_1_lt));
  not not_2 (not_2_out, LEA_ID_RR);
  or or_4 (or_4_out, comparator_1_eq, comparator_1_lt);
  Multiplexer #(.width(32), .disabled(0), .enable("false")) multiplexer_5 (
    .in0(GOTO_PC_Value_PCaddr24), .in1(RET_PC_Value__ra), .out(multiplexer_5_out), .sel(not_2_out));
  Multiplexer #(.width(32), .disabled(0), .enable("false")) multiplexer_6 (
    .in0(CALL_PC_Value__tr), .in1(Offset20_ID_RR), .out(OUT_2_ID_RR), .sel(I_Type));
  or or_5 (or_5_out, comparator_1_gt, comparator_1_lt);
  Multiplexer #(.disabled(0), .enable("false")) multiplexer_7 (
    .in0(or_5_out), .in1(or_4_out), .out(SKP__ID_RR), .sel(Instruction_ID_RR_In[24]));
  not not_3 (not_3_out, PC_SELECTOR_ID_RR[2]);
  Multiplexer #(.width(32), .disabled(0), .enable("false")) multiplexer_8 (
    .in0(PC_ID_RR_In), .in1(multiplexer_5_out), .out(OUT_1_ID_RR), .sel(not_3_out));

  assign Opcode_ID_RR = Instruction_ID_RR_In[31:28];
  assign PC_ID_RR_Out = PC_ID_RR_In;
  assign PCaddr24_ID_RR = GOTO_PC_Value_PCaddr24;
  assign RX_ID_RR = Instruction_ID_RR_In[27:24];
  assign RY_ID_RR = Instruction_ID_RR_In[23:20];
  assign RZ_ID_RR = Instruction_ID_RR_In[3:0];

  // Other names for the same wires on the sheet: Instruction_ID_RR[31:0] = Instruction_ID_RR_In;
  //   Unused_ID_RR[15:0] = Instruction_ID_RR_In[19:4]; ID_RR_Out_RegNo1[31:0] = OUT_1_ID_RR;
  //   ID_RR_Out_RegNo2[31:0] = OUT_2_ID_RR; GOTO_ID_RR = PC_SELECTOR_ID_RR[1]; CALL_ID_RR = PC_SELECTOR_ID_RR[2];
  //   RET_ID_RR = PC_SELECTOR_ID_RR[3]; HALT_ID_RR = PC_SELECTOR_ID_RR[4]; ra[31:0] = RET_PC_Value__ra;
  //   tr[31:0] = CALL_PC_Value__tr
endmodule

// EX
module EX_Stage (
  input  [31:0] RDATA1_EX,
  input  [31:0] RDATA2_EX,
  input  [3:0] Opcode_EX,
  input  [31:0] OFFSET_EX,
  input  [3:0] RX_EX,
  output [31:0] RDATA1_EX_2,
  output [31:0] EX_RESULT,
  output [31:0] RDATA2_EX_2,
  output [3:0] Opcode_EX_2,
  output [31:0] OFFSET_EX_2,
  output [3:0] RX_EX_2
);

  wire ADD_EX, ADD_OFFSET20, ADDI_EX, CALL_EX, GOTO_EX, HALT_EX, LEA_EX, LW_EX, NAND_EX, not_1_out, or_2_out,
       RET_EX, SKP_EX, SW_EX;
  wire [31:0] adder_1_out, multiplexer_1_out, multiplexer_2_out, nand_1_out;

  Decoder #(.select(4), .enable("false")) decoder_1 (
    .out0(ADD_EX), .out1(ADDI_EX), .out2(NAND_EX), .out3(SKP_EX), .out4(GOTO_EX), .out5(LEA_EX),
    .out8(LW_EX), .out9(SW_EX), .out12(CALL_EX), .out13(RET_EX), .out14(HALT_EX), .sel(Opcode_EX));  // open: out6, out7, out10, out11, out15
  Adder #(.width(32)) adder_1 (.a(RDATA1_EX), .b(multiplexer_1_out), .out(adder_1_out));  // open: cin, cout
  Multiplexer #(.width(32), .disabled(0), .enable("false")) multiplexer_1 (
    .in0(RDATA2_EX), .in1(OFFSET_EX), .out(multiplexer_1_out), .sel(ADD_OFFSET20));
  assign nand_1_out = ~(RDATA1_EX & RDATA2_EX);  // NAND_Gate nand_1, 32 bits wide
  or or_1 (ADD_OFFSET20, ADDI_EX, SW_EX, LW_EX);
  Multiplexer #(.width(32), .disabled(0), .enable("false")) multiplexer_2 (
    .in0(adder_1_out), .in1(nand_1_out), .out(multiplexer_2_out), .sel(NAND_EX));
  Multiplexer #(.width(32), .disabled(0), .enable("false")) multiplexer_3 (
    .in0(RDATA1_EX), .in1(multiplexer_2_out), .out(EX_RESULT), .sel(not_1_out));
  not not_1 (not_1_out, or_2_out);
  or or_2 (or_2_out, CALL_EX, LEA_EX);

  assign OFFSET_EX_2 = OFFSET_EX;
  assign Opcode_EX_2 = Opcode_EX;
  assign RDATA1_EX_2 = RDATA1_EX;
  assign RDATA2_EX_2 = RDATA2_EX;
  assign RX_EX_2 = RX_EX;

  // Other names for the same wires on the sheet: EX_OFFSET20[31:0] = OFFSET_EX
endmodule

// MEM
module MEM_Stage (
  input  CLK,
  input  [3:0] Opcode_MEM,
  input  [3:0] RX_MEM,
  input  [3:0] RY_MEM,
  input  [31:0] RDATA1_MEM_In,
  input  [31:0] RDATA2_MEM_In,
  input  [31:0] RESULT_MEM_In,
  output [3:0] Opcode_MEM_OUT,
  output [3:0] RX_MEM_OUT,
  output [31:0] RAM_MEM_OUT
);

  wire ADD_MEM, ADDI_MEM, CALL_MEM, GOTO_MEM, HALT_MEM, LEA_MEM, LW_MEM, NAND_MEM, RET_MEM, SKP_MEM, SW_MEM;
  wire [23:0] bit_extender_1_out;
  wire [31:0] ram_1_data;

  Bit_Extender #(.in_width(32), .out_width(24)) bit_extender_1 (.in(RESULT_MEM_In), .out(bit_extender_1_out));
  RAM #(.addrWidth(24), .dataWidth(32), .bus("separate")) ram_1 (
    .addr(bit_extender_1_out), .din(RDATA2_MEM_In), .data(ram_1_data), .str(SW_MEM), .clk(CLK));  // open: sel, ld, clr
  Multiplexer #(.width(32), .disabled(0), .enable("false")) multiplexer_1 (
    .in0(RESULT_MEM_In), .in1(ram_1_data), .out(RAM_MEM_OUT), .sel(LW_MEM));
  Decoder #(.select(4), .enable("false")) decoder_1 (
    .out0(ADD_MEM), .out1(ADDI_MEM), .out2(NAND_MEM), .out3(SKP_MEM), .out4(GOTO_MEM), .out5(LEA_MEM),
    .out8(LW_MEM), .out9(SW_MEM), .out12(CALL_MEM), .out13(RET_MEM), .out14(HALT_MEM), .sel(Opcode_MEM));  // open: out6, out7, out10, out11, out15

  assign Opcode_MEM_OUT = Opcode_MEM;
  assign RX_MEM_OUT = RX_MEM;

  // Other names for the same wires on the sheet: RAM_MEM[31:0] = RAM_MEM_OUT; RDATA1_MEM[31:0] = RDATA1_MEM_In;
  //   RDATA2_MEM[31:0] = RDATA2_MEM_In; RESULT_MEM[31:0] = RESULT_MEM_In

  // Notes on the sheet:
  //   MEM
endmodule

// WB
module WB_Stage (
  input  CLK,
  input  [3:0] RX,
  input  [3:0] OPCODE_WB,
  input  [31:0] WB_Data,
  output [3:0] OPCODE_WB_OUT,
  output [3:0] REG_WB,
  output [31:0] WB_Data_2,
  output WB
);

  wire ADD, ADDI, CALL, comparator_1_eq, GOTO, HALT, LEA, LW, NAND, RET, SKP, SW;

  or or_1 (WB, ADD, ADDI, NAND, LEA, LW, CALL);
  Decoder #(.select(4), .enable("false")) decoder_1 (
    .out0(ADD), .out1(ADDI), .out2(NAND), .out3(SKP), .out4(GOTO), .out5(LEA), .out8(LW), .out9(SW),
    .out12(CALL), .out13(RET), .out14(HALT), .sel(OPCODE_WB));  // open: out6, out7, out10, out11, out15
  Multiplexer #(.width(4), .disabled(0), .enable("false")) multiplexer_1 (
    .in0(RX), .in1(4'b1111), .out(REG_WB), .sel(comparator_1_eq));
  Comparator #(.width(4), .mode("unsigned")) comparator_1 (
    .a(OPCODE_WB), .b(4'b1100), .eq(comparator_1_eq));  // open: gt, lt

  assign OPCODE_WB_OUT = OPCODE_WB;
  assign WB_Data_2 = WB_Data;

  // Notes on the sheet:
  //   WB
endmodule

// IDRR/EX
module IDRR_EX_Buffer_Fixed (
  input  CLK,
  input  CLEAR,
  input  IDRR_STALL,
  input  [31:0] PC_In,
  input  [31:0] OFFSET_IN,
  input  [31:0] RData1_IN,
  input  [31:0] RData2_IN,
  input  [31:0] PCADDR24_IN,
  input  [3:0] OPCODE_IN,
  input  [3:0] RX_IN,
  input  [3:0] RY_IN,
  input  [3:0] RZ_IN,
  output [31:0] PC_Out,
  output [31:0] OFFSET_OUT,
  output [31:0] RData1_OUT,
  output [31:0] RData2_OUT,
  output [31:0] PCADDR24_OUT,
  output [3:0] OPCODE_OUT,
  output [3:0] RX_OUT,
  output [3:0] RY_OUT,
  output [3:0] RZ_OUT
);

  wire not_1_out;
  wire [3:0] Opcode_q, Rx_q, RY_q, RZ_q;
  wire [31:0] Instruction_q, PC_q, PCADDR24_q, RData1_q, RData2_q;

  not not_1 (not_1_out, IDRR_STALL);
  Register #(.width(32)) PC (.D(PC_In), .en(not_1_out), .Q(PC_q), .clk(CLK), .clr(CLEAR));
  Register #(.width(32)) Instruction (.D(OFFSET_IN), .en(not_1_out), .Q(Instruction_q), .clk(CLK), .clr(CLEAR));
  Register #(.width(32)) RData1 (.D(RData1_IN), .en(not_1_out), .Q(RData1_q), .clk(CLK), .clr(CLEAR));
  Register #(.width(32)) RData2 (.D(RData2_IN), .en(not_1_out), .Q(RData2_q), .clk(CLK), .clr(CLEAR));
  Register #(.width(32)) PCADDR24 (.D(PCADDR24_IN), .en(not_1_out), .Q(PCADDR24_q), .clk(CLK), .clr(CLEAR));
  Register #(.width(4)) Opcode (.D(OPCODE_IN), .en(not_1_out), .Q(Opcode_q), .clk(CLK), .clr(CLEAR));
  Register #(.width(4)) Rx (.D(RX_IN), .en(not_1_out), .Q(Rx_q), .clk(CLK), .clr(CLEAR));
  Register #(.width(4)) RY (.D(RY_IN), .en(not_1_out), .Q(RY_q), .clk(CLK), .clr(CLEAR));
  Register #(.width(4)) RZ (.D(RZ_IN), .en(not_1_out), .Q(RZ_q), .clk(CLK), .clr(CLEAR));
  Multiplexer #(.width(32), .disabled(0), .enable("false")) multiplexer_1 (
    .in0(PC_q), .in1({32{1'b0}}), .out(PC_Out), .sel(IDRR_STALL));
  Multiplexer #(.width(32), .disabled(0), .enable("false")) multiplexer_2 (
    .in0(Instruction_q), .in1({32{1'b0}}), .out(OFFSET_OUT), .sel(IDRR_STALL));
  Multiplexer #(.width(32), .disabled(0), .enable("false")) multiplexer_3 (
    .in0(RData1_q), .in1({32{1'b0}}), .out(RData1_OUT), .sel(IDRR_STALL));
  Multiplexer #(.width(32), .disabled(0), .enable("false")) multiplexer_4 (
    .in0(RData2_q), .in1({32{1'b0}}), .out(RData2_OUT), .sel(IDRR_STALL));
  Multiplexer #(.width(32), .disabled(0), .enable("false")) multiplexer_5 (
    .in0(PCADDR24_q), .in1({32{1'b0}}), .out(PCADDR24_OUT), .sel(IDRR_STALL));
  Multiplexer #(.width(4), .disabled(0), .enable("false")) multiplexer_6 (
    .in0(Opcode_q), .in1(4'b0000), .out(OPCODE_OUT), .sel(IDRR_STALL));
  Multiplexer #(.width(4), .disabled(0), .enable("false")) multiplexer_7 (
    .in0(Rx_q), .in1(4'b0000), .out(RX_OUT), .sel(IDRR_STALL));
  Multiplexer #(.width(4), .disabled(0), .enable("false")) multiplexer_8 (
    .in0(RY_q), .in1(4'b0000), .out(RY_OUT), .sel(IDRR_STALL));
  Multiplexer #(.width(4), .disabled(0), .enable("false")) multiplexer_9 (
    .in0(RZ_q), .in1(4'b0000), .out(RZ_OUT), .sel(IDRR_STALL));
endmodule
