// Logisim project Conte-200 (3).circ as structural Verilog: 5 circuits, main circuit Datapath
module Datapath (
  input  reset,
  output [3:0] RX,
  output [3:0] RY,
  output [3:0] RZ,
  output [3:0] OP,
  output Z,
  output [1:0] out_7,
  output [31:0] out_8,
  output [31:0] out_9,
  output [31:0] Value_on_Bus,
  output [3:0] out_11,
  output out_12,
  output out_13,
  output [5:0] out_14
);

  wire ChkCmp, CLK, comparator_1_eq, comparator_1_lt, DrADDR, DrALU, DrMEM, DrOFF, DrPC, DrREG, LdA, LdB,
       LdCmp, LdIR, LdMAR, LdPC, multiplexer_1_out, not_1_out, OPTest, or_1_out, RegSelHi, RegSelLo, WrMEM,
       WrREG;
  wire [3:0] OP_t, RX_t, RY_t, RZ_t;
  wire [5:0] multiplexer_2_out, NextState, opOut, zOut;
  wire [19:4] IR_q;
  wire [23:0] MAR_q, n24truncate_1_out_2;
  wire [31:0] A_q, alu_1_out_4, B_q, bit_extender_1_out, PC_q, ram_1_data, RegFile_out_6;

  Register #(.width(32)) PC (.D(out_9), .en(LdPC), .Q(PC_q), .clk(CLK), .clr(reset));
  assign out_9 = DrPC ? PC_q : 32'bz;  // Controlled_Buffer controlled_buffer_1
  Register #(.width(32)) A (.D(out_9), .en(LdA), .Q(A_q), .clk(CLK), .clr(reset));
  ROM #(.addrWidth(6), .dataWidth(26)) rom_1 (
    .addr(out_14),
    .data({ChkCmp, OPTest, out_7, RegSelHi, RegSelLo, WrMEM, WrREG, LdCmp, LdB, LdA, LdMAR, LdIR, LdPC, DrADDR, DrOFF, DrPC, DrALU, DrMEM, DrREG, NextState}));  // open: sel
  ROM #(.addrWidth(4), .dataWidth(6)) rom_2 (.addr(OP_t), .data(opOut));  // open: sel
  ROM #(.addrWidth(2), .dataWidth(6)) rom_3 (.addr({1'b0, out_12}), .data(zOut));  // open: sel
  Register #(.width(32)) B (.D(out_9), .en(LdB), .Q(B_q), .clk(CLK), .clr(reset));
  ALU alu_1 (.in_1(out_7), .A(A_q), .B(B_q), .out_4(alu_1_out_4));
  assign out_9 = DrALU ? alu_1_out_4 : 32'bz;  // Controlled_Buffer controlled_buffer_2
  Comparator #(.width(32)) comparator_1 (
    .a(out_9), .b({32{1'b0}}), .eq(comparator_1_eq), .lt(comparator_1_lt));  // open: gt
  // Probe on out_11
  not not_1 (not_1_out, comparator_1_eq);
  Multiplexer #(.disabled(0), .enable("false")) multiplexer_1 (
    .in0(not_1_out), .in1(or_1_out), .out(multiplexer_1_out), .sel(RX_t[0]));
  or or_1 (or_1_out, comparator_1_eq, comparator_1_lt);
  Clock clock_1 (.out(CLK));
  RegisterFile RegFile (.regno(out_11), .CLK(CLK), .Din(out_9), .reset(reset), .WrREG(WrREG), .out_6(RegFile_out_6));
  assign out_9 = DrREG ? RegFile_out_6 : 32'bz;  // Controlled_Buffer controlled_buffer_3
  Register #(.width(1)) u_Z (.D(multiplexer_1_out), .en(LdCmp), .Q(out_12), .clk(CLK), .clr(reset));
  _24Truncate u_24truncate_1 (.in_1(out_9), .out_2(n24truncate_1_out_2));
  Register #(.width(24)) MAR (.D(n24truncate_1_out_2), .en(LdMAR), .Q(MAR_q), .clk(CLK), .clr(reset));
  RAM #(.addrWidth(24), .dataWidth(32), .bus("separate")) ram_1 (
    .addr(MAR_q), .din(out_9), .data(ram_1_data), .str(WrMEM), .clk(CLK), .clr(reset));  // open: sel, ld
  Register #(.width(32)) IR (.D(out_9), .en(LdIR), .Q({OP_t, RX_t, RY_t, IR_q, RZ_t}), .clk(CLK), .clr(reset));
  assign out_9 = DrMEM ? ram_1_data : 32'bz;  // Controlled_Buffer controlled_buffer_4
  Multiplexer #(.select(2), .width(6), .disabled(0), .enable("false")) multiplexer_2 (
    .in0(NextState), .in1(opOut), .in2(zOut), .out(multiplexer_2_out), .sel({ChkCmp, OPTest}));  // open: in3
  assign bit_extender_1_out = {{12{1'b0}}, {IR_q, RZ_t}};  // Bit_Extender bit_extender_1
  assign out_9 = DrOFF ? bit_extender_1_out : 32'bz;  // Controlled_Buffer controlled_buffer_5
  Register #(.width(6)) State_Register (.D(multiplexer_2_out), .Q(out_14), .clk(CLK), .clr(reset));  // open: en
  // Probe on RX_t
  assign out_8 = {{8{1'b0}}, {RY_t, IR_q, RZ_t}};  // Bit_Extender bit_extender_2
  assign out_9 = DrADDR ? out_8 : 32'bz;  // Controlled_Buffer controlled_buffer_6
  Multiplexer #(.select(2), .width(4), .disabled(0), .enable("false")) multiplexer_3 (
    .in0(RX_t), .in1(RY_t), .in2(RZ_t), .in3(4'b1111), .out(out_11), .sel({RegSelHi, RegSelLo}));
  // AND_Gate and_1 is placed but not wired
  // AND_Gate and_2 is placed but not wired

  assign out_13 = out_7[0];
  assign Value_on_Bus = out_9;

  // Other names for the same wires on the sheet: Z_t = out_12; ALULo = out_7[0]; func[1:0] = out_7; ALUHi = out_7[1];
  //   regno[3:0] = out_11; state[5:0] = out_14

  // Notes on the sheet:
  //   Main ROM
  //   Sequencer ROM
  //   Condition ROM
  //   contents of rom_1 (hex, n*v repeats v):
  //   c201 2082 1c01100 108044 210045 40100 108047 10408 40100 10804a 21004b 840100 10804d 1040e 410f
  //   40080 108051 10412 4113 80040 108055 210056 420117 2000000 8219 c01100 0 1b 1800 40800 34021f 1040
  //   301040
  //   contents of rom_2 (hex, n*v repeats v):
  //   3 6 9 14 1c 1d 0 0 c 10 0 0 1e 20 0 1b
  //   contents of rom_3 (hex, n*v repeats v):
  //   0 18
  //   LC-2200 Datapath by Ashwini Iyer
  //   RegSel
endmodule

module ALU (
  input  [1:0] in_1,
  input  [31:0] A,
  input  [31:0] B,
  output [31:0] out_4
);

  wire [31:0] adder_1_out, adder_2_out, nand_1_out, subtractor_1_out;

  Adder #(.width(32)) adder_1 (.a(A), .b(B), .out(adder_1_out));  // open: cin, cout
  Subtractor #(.width(32)) subtractor_1 (.a(A), .b(B), .out(subtractor_1_out));  // open: bin, bout
  assign nand_1_out = ~(A & B);  // NAND_Gate nand_1, 32 bits wide
  Adder #(.width(32)) adder_2 (.a(A), .b(32'h1), .out(adder_2_out));  // open: cin, cout
  Multiplexer #(.select(2), .width(32), .disabled(0), .enable("false")) multiplexer_1 (
    .in0(adder_1_out), .in1(subtractor_1_out), .in2(nand_1_out), .in3(adder_2_out), .out(out_4), .sel(in_1));

  // Other names for the same wires on the sheet: func[1:0] = in_1; output[31:0] = out_4
endmodule

module _24Truncate (
  input  [31:0] in_1,
  output [23:0] out_2
);


  assign out_2 = in_1[23:0];
endmodule

module RegisterFile (
  input  [3:0] regno,
  input  CLK,
  input  [31:0] Din,
  input  reset,
  input  WrREG,
  output [31:0] out_6
);

  wire and_1_out, and_2_out, and_4_out, and_5_out, and_6_out, and_7_out, and_8_out, and_9_out, and_10_out,
       and_11_out, and_12_out, and_13_out, and_14_out, and_15_out, and_16_out, decoder_1_out0,
       decoder_1_out1, decoder_1_out2, decoder_1_out3, decoder_1_out4, decoder_1_out5, decoder_1_out6,
       decoder_1_out7, decoder_1_out8, decoder_1_out9, decoder_1_out10, decoder_1_out11, decoder_1_out12,
       decoder_1_out13, decoder_1_out14, decoder_1_out15;
  wire [31:0] register_1_q, register_2_q, register_3_q, register_4_q, register_5_q, register_6_q,
       register_7_q, register_8_q, register_9_q, register_10_q, register_11_q, register_12_q, register_13_q,
       register_14_q, register_15_q, register_16_q;

  Decoder #(.select(4), .enable("false")) decoder_1 (
    .out0(decoder_1_out0), .out1(decoder_1_out1), .out2(decoder_1_out2), .out3(decoder_1_out3),
    .out4(decoder_1_out4), .out5(decoder_1_out5), .out6(decoder_1_out6), .out7(decoder_1_out7),
    .out8(decoder_1_out8), .out9(decoder_1_out9), .out10(decoder_1_out10), .out11(decoder_1_out11),
    .out12(decoder_1_out12), .out13(decoder_1_out13), .out14(decoder_1_out14), .out15(decoder_1_out15),
    .sel(regno));
  and and_1 (and_1_out, decoder_1_out14, WrREG);
  and and_2 (and_2_out, decoder_1_out15, WrREG);
  // AND_Gate and_3 has open pins: in0=decoder_1_out0, in1=WrREG, out=open
  and and_4 (and_4_out, decoder_1_out1, WrREG);
  and and_5 (and_5_out, decoder_1_out2, WrREG);
  and and_6 (and_6_out, decoder_1_out3, WrREG);
  and and_7 (and_7_out, decoder_1_out4, WrREG);
  and and_8 (and_8_out, decoder_1_out5, WrREG);
  and and_9 (and_9_out, decoder_1_out6, WrREG);
  and and_10 (and_10_out, decoder_1_out7, WrREG);
  and and_11 (and_11_out, decoder_1_out8, WrREG);
  and and_12 (and_12_out, decoder_1_out9, WrREG);
  and and_13 (and_13_out, decoder_1_out10, WrREG);
  and and_14 (and_14_out, decoder_1_out11, WrREG);
  and and_15 (and_15_out, decoder_1_out12, WrREG);
  and and_16 (and_16_out, decoder_1_out13, WrREG);
  Register #(.width(32)) register_1 (.D(Din), .en(1'b0), .Q(register_1_q), .clk(CLK), .clr(reset));
  Register #(.width(32)) register_2 (.D(Din), .en(and_4_out), .Q(register_2_q), .clk(CLK), .clr(reset));
  Register #(.width(32)) register_3 (.D(Din), .en(and_5_out), .Q(register_3_q), .clk(CLK), .clr(reset));
  Register #(.width(32)) register_4 (.D(Din), .en(and_6_out), .Q(register_4_q), .clk(CLK), .clr(reset));
  Register #(.width(32)) register_5 (.D(Din), .en(and_7_out), .Q(register_5_q), .clk(CLK), .clr(reset));
  Register #(.width(32)) register_6 (.D(Din), .en(and_8_out), .Q(register_6_q), .clk(CLK), .clr(reset));
  Register #(.width(32)) register_7 (.D(Din), .en(and_9_out), .Q(register_7_q), .clk(CLK), .clr(reset));
  Register #(.width(32)) register_8 (.D(Din), .en(and_10_out), .Q(register_8_q), .clk(CLK), .clr(reset));
  Register #(.width(32)) register_9 (.D(Din), .en(and_11_out), .Q(register_9_q), .clk(CLK), .clr(reset));
  Register #(.width(32)) register_10 (.D(Din), .en(and_12_out), .Q(register_10_q), .clk(CLK), .clr(reset));
  Register #(.width(32)) register_11 (.D(Din), .en(and_13_out), .Q(register_11_q), .clk(CLK), .clr(reset));
  Register #(.width(32)) register_12 (.D(Din), .en(and_14_out), .Q(register_12_q), .clk(CLK), .clr(reset));
  Register #(.width(32)) register_13 (.D(Din), .en(and_15_out), .Q(register_13_q), .clk(CLK), .clr(reset));
  Register #(.width(32)) register_14 (.D(Din), .en(and_16_out), .Q(register_14_q), .clk(CLK));  // open: clr
  Register #(.width(32)) register_15 (.D(Din), .en(and_1_out), .Q(register_15_q), .clk(CLK), .clr(reset));
  Register #(.width(32)) register_16 (.D(Din), .en(and_2_out), .Q(register_16_q), .clk(CLK), .clr(reset));
  Multiplexer #(.select(4), .width(32), .disabled(0), .enable("false")) multiplexer_1 (
    .in0(register_1_q), .in1(register_2_q), .in2(register_3_q), .in3(register_4_q), .in4(register_5_q),
    .in5(register_6_q), .in6(register_7_q), .in7(register_8_q), .in8(register_9_q), .in9(register_10_q),
    .in10(register_11_q), .in11(register_12_q), .in12(register_13_q), .in13(register_14_q),
    .in14(register_15_q), .in15(register_16_q), .out(out_6), .sel(regno));

  // Other names for the same wires on the sheet: Clock = CLK; dOut[31:0] = out_6
endmodule

module Microcontrol_Unit (
  input  [3:0] OP,
  input  Z,
  input  reset,
  input  CLK,
  output DrREG,
  output LdPC,
  output WrREG,
  output OPTest,
  output DrMEM,
  output LdIR,
  output WrMEM,
  output ChkCmp,
  output DrALU,
  output LdMAR,
  output RegSelLo,
  output DrPC,
  output LdA,
  output RegSelHi,
  output DrOFF,
  output LdB,
  output ALULo,
  output [5:0] state,
  output DrADDR,
  output LdCmp,
  output ALUHi
);

  wire [5:0] multiplexer_1_out, NextState, opOut, zOut;

  ROM #(.addrWidth(6), .dataWidth(26)) rom_1 (
    .addr(state),
    .data({ChkCmp, OPTest, ALUHi, ALULo, RegSelHi, RegSelLo, WrMEM, WrREG, LdCmp, LdB, LdA, LdMAR, LdIR, LdPC, DrADDR, DrOFF, DrPC, DrALU, DrMEM, DrREG, NextState}));  // open: sel
  ROM #(.addrWidth(4), .dataWidth(6)) rom_2 (.addr(OP), .data(opOut));  // open: sel
  ROM #(.addrWidth(2), .dataWidth(6)) rom_3 (.addr({1'b0, Z}), .data(zOut));  // open: sel
  Multiplexer #(.select(2), .width(6), .disabled(0), .enable("false")) multiplexer_1 (
    .in0(NextState), .in1(opOut), .in2(zOut), .out(multiplexer_1_out), .sel({ChkCmp, OPTest}));  // open: in3
  Register #(.width(6)) State_Register (.D(multiplexer_1_out), .Q(state), .clk(CLK), .clr(reset));  // open: en

  // Notes on the sheet:
  //   Main ROM
  //   Sequencer ROM
  //   Condition ROM
  //   contents of rom_1 (hex, n*v repeats v):
  //   c201 2082 1c01100 108044 210045 40100 108047 10408 40100 10804a 21004b 440100 10804d 1040e 410f
  //   40080 108051 10412 4113 80040 8055 110056 820117 2000000 8219 1041a 1100 1b 1800 40800 34021f 1040
  //   301040
  //   contents of rom_2 (hex, n*v repeats v):
  //   3 6 9 12*0 1b
endmodule
